# Fritzing sketch wiring (saved by Fritzing 0.9.3b)
breadboards: 1

parts:
  Part1 = Arduino Pro Mini v13
  U1 = SUP500F [package=sup500f]
  Grove1 = Grove OLED 128x96
  R1 = Resistor [tolerance=±5% resistance=100 package="2010 [SMD]"]
  R2 = Resistor [tolerance=±5% resistance=1.5k package="2010 [SMD]"]
  R3 = Resistor [tolerance=±5% resistance=1.5k package="2010 [SMD]"]
  LED1 = smd LED [color="Red (633nm)" package="0805 [SMD]"]
  LED2 = smd LED [color="Blue (505nm)" package="0805 [SMD]"]
  J1 = Piezo Speaker
  S1 = Toggle Switch [package=THT]
  S2 = Pushbutton [package="[THT]"]
  R4 = Resistor [tolerance=±5% resistance=10k package="2010 [SMD]"]

nets:
  VCC: Part1.VCC, U1.TX-O, Grove1.VCC, R2.Pin_1, S2.Pin_3, S2.Pin_4
  N1: Part1.A4, Grove1.SDA
  N2: Part1.A5, Grove1.SCL
  N3: Part1.RAW, S1.COM
  GND: Part1.GND, U1.RX-I, Grove1.GND, LED1.cathode, LED2.cathode, J1.pin1, S1.L1, R4.Pin_1
  N4: Part1.D7, S2.Pin_1, S2.Pin_2, R4.Pin_0
  N5: Part1.D5_PWM, U1.VCC
  N6: Part1.D4, U1.GND
  N7: Part1.D3_PWM, R1.Pin_0
  N8: Part1.D2, R3.Pin_1
  N9: R1.Pin_1, J1.pin2
  N10: R2.Pin_0, LED1.anode
  N11: R3.Pin_0, LED2.anode

notes:
  input power - 5V
  piezo buzzer
  NEO 6M gps module
  SSD1306 IC2 OLED display
  Arduino Pro Mini 5V
